// Logisim project procesador_xavi.circ as structural Verilog: 13 circuits, main circuit main
module main (
  input  in_1,
  input  in_2
);

  wire alu_1_c_out, alu_1_ov_out, alu_1_sg_out, alu_1_z_out, ALU_ON, clk_1_clk_out, clock_1_out,
       decoder_1_out0, decoder_1_out1, decoder_1_out2, decoder_1_out3, decoder_1_out4, decoder_1_out5,
       INPUT_OUT, JUMP, MAR_IN, MAR_OUT, not_1_out, or_1_out, OUT_REG_IN, OUT_REG_OUT, PC_ON, PC_OUT,
       REG_A_IN, REG_A_OUT, REG_B_IN, REG_B_OUT, RESET, WRITE_RAM_ENB;
  wire [2:0] ALU_OP, STEP_COUNT;
  wire [3:3] step_counter_1_step_counter_out;
  wire [7:0] alu_1_out_8, ALU_A, ALU_B, binary_to_bcd_converter_2_p1, INST_LOAD, ram_memory_1_out_5,
       register_output_1_always_out;
  wire [15:0] mar_1_mar_out, pc_1_always_out;

  PC pc_1 (
    .JUMP(JUMP), .COUNTER_ENB(PC_ON), .CLK(clk_1_clk_out), .ADD_IN(mar_1_mar_out), .OUT_ENB(PC_OUT),
    .RESET(RESET), .ALWAYS_OUT(pc_1_always_out));  // open: PC_OUT
  MAR mar_1 (
    .DATA_IN(pc_1_always_out), .ENB_IN(MAR_IN), .CLK(clk_1_clk_out), .RESET(RESET), .ENB_OUT(MAR_OUT),
    .MAR_OUT(mar_1_mar_out));  // open: ALWAYS_OUT
  LED led_1 (.in(pc_1_always_out[15]));
  LED led_2 (.in(pc_1_always_out[14]));
  LED led_3 (.in(pc_1_always_out[13]));
  LED led_4 (.in(pc_1_always_out[12]));
  Pull_Resistor pull_resistor_1 (.node(pc_1_always_out[15]));
  Pull_Resistor pull_resistor_2 (.node(pc_1_always_out[14]));
  Pull_Resistor pull_resistor_3 (.node(pc_1_always_out[13]));
  Pull_Resistor pull_resistor_4 (.node(pc_1_always_out[12]));
  LED led_5 (.in(pc_1_always_out[11]));
  LED led_6 (.in(pc_1_always_out[10]));
  LED led_7 (.in(pc_1_always_out[9]));
  LED led_8 (.in(pc_1_always_out[8]));
  Pull_Resistor pull_resistor_5 (.node(pc_1_always_out[11]));
  Pull_Resistor pull_resistor_6 (.node(pc_1_always_out[10]));
  Pull_Resistor pull_resistor_7 (.node(pc_1_always_out[9]));
  Pull_Resistor pull_resistor_8 (.node(pc_1_always_out[8]));
  LED led_9 (.in(pc_1_always_out[7]));
  LED led_10 (.in(pc_1_always_out[6]));
  LED led_11 (.in(pc_1_always_out[5]));
  LED led_12 (.in(pc_1_always_out[4]));
  Pull_Resistor pull_resistor_9 (.node(pc_1_always_out[7]));
  Pull_Resistor pull_resistor_10 (.node(pc_1_always_out[6]));
  Pull_Resistor pull_resistor_11 (.node(pc_1_always_out[5]));
  Pull_Resistor pull_resistor_12 (.node(pc_1_always_out[4]));
  LED led_13 (.in(pc_1_always_out[3]));
  LED led_14 (.in(pc_1_always_out[2]));
  LED led_15 (.in(pc_1_always_out[1]));
  LED led_16 (.in(pc_1_always_out[0]));
  Pull_Resistor pull_resistor_13 (.node(pc_1_always_out[3]));
  Pull_Resistor pull_resistor_14 (.node(pc_1_always_out[2]));
  Pull_Resistor pull_resistor_15 (.node(pc_1_always_out[1]));
  Pull_Resistor pull_resistor_16 (.node(pc_1_always_out[0]));
  Button u_RESET (.out(RESET));
  RAM_MEMORY ram_memory_1 (
    .ADD_IN(pc_1_always_out), .WRITE_ENB(WRITE_RAM_ENB), .CLK(clk_1_clk_out), .DATA_IN(INST_LOAD),
    .out_5(ram_memory_1_out_5));
  LED led_17 (.in(ram_memory_1_out_5[7]));
  LED led_18 (.in(ram_memory_1_out_5[6]));
  LED led_19 (.in(ram_memory_1_out_5[5]));
  LED led_20 (.in(ram_memory_1_out_5[4]));
  Clock clock_1 (.out(clock_1_out));
  FLAGS_REGISTER flags_register_1 (
    .CLK(clk_1_clk_out), .C_ALU(alu_1_c_out), .Z_ALU(alu_1_z_out), .SG_ALU(alu_1_sg_out),
    .OV_ALU(alu_1_ov_out));  // open: FLAG_EN, C_OUT, Z_OUT, SG_OUT, OV_OUT
  LED led_21 (.in(ram_memory_1_out_5[3]));
  LED led_22 (.in(ram_memory_1_out_5[2]));
  LED led_23 (.in(ram_memory_1_out_5[1]));
  LED led_24 (.in(ram_memory_1_out_5[0]));
  CLK clk_1 (.CLK_IN(clock_1_out), .CLK_ENB(in_1), .MANUAL(in_2), .CLK_OUT(clk_1_clk_out));  // open: STOP
  ALU alu_1 (
    .OPERATION(ALU_OP), .A_IN(ALU_A), .B_IN(ALU_B), .ENB_OUT(ALU_ON), .out_8(alu_1_out_8),
    .C_OUT(alu_1_c_out), .SG_OUT(alu_1_sg_out), .OV_OUT(alu_1_ov_out), .Z_OUT(alu_1_z_out));  // open: C_IN, out_7
  CONTROL_UNIT control_unit_1 (
    .in_1(ram_memory_1_out_5), .STEP_COUNT(STEP_COUNT), .ALU_OP(ALU_OP), .JUMP(JUMP), .ALU_ON(ALU_ON),
    .PC_ON(PC_ON), .REG_A_IN(REG_A_IN), .REG_B_IN(REG_B_IN), .MAR_IN(MAR_IN), .OUT_REG_IN(OUT_REG_IN),
    .REG_A_OUT(REG_A_OUT), .REG_B_OUT(REG_B_OUT), .MAR_OUT(MAR_OUT), .OUT_REG_OUT(OUT_REG_OUT),
    .INPUT_OUT(INPUT_OUT), .PC_OUT(PC_OUT), .RAM_READ_ENB(WRITE_RAM_ENB));  // open: INS_REG_IN, INS_REG_OUT
  LED led_25 (.in(alu_1_out_8[7]));
  LED led_26 (.in(alu_1_out_8[6]));
  LED led_27 (.in(alu_1_out_8[5]));
  Pull_Resistor pull_resistor_17 (.node(alu_1_out_8[7]));
  Pull_Resistor pull_resistor_18 (.node(alu_1_out_8[6]));
  Pull_Resistor pull_resistor_19 (.node(alu_1_out_8[5]));
  LED led_28 (.in(alu_1_out_8[4]));
  LED led_29 (.in(alu_1_out_8[3]));
  LED led_30 (.in(alu_1_out_8[2]));
  LED led_31 (.in(alu_1_out_8[1]));
  Pull_Resistor pull_resistor_20 (.node(alu_1_out_8[4]));
  Pull_Resistor pull_resistor_21 (.node(alu_1_out_8[3]));
  Pull_Resistor pull_resistor_22 (.node(alu_1_out_8[2]));
  Pull_Resistor pull_resistor_23 (.node(alu_1_out_8[1]));
  LED led_32 (.in(decoder_1_out0));
  LED led_33 (.in(decoder_1_out1));
  LED led_34 (.in(alu_1_out_8[0]));
  Pull_Resistor pull_resistor_24 (.node(alu_1_out_8[0]));
  LED led_35 (.in(decoder_1_out2));
  LED led_36 (.in(decoder_1_out3));
  LED led_37 (.in(decoder_1_out4));
  Decoder #(.enable("false"), .select(3)) decoder_1 (
    .out0(decoder_1_out0), .out1(decoder_1_out1), .out2(decoder_1_out2), .out3(decoder_1_out3),
    .out4(decoder_1_out4), .out5(decoder_1_out5), .sel(STEP_COUNT));  // open: out6, out7
  assign alu_1_out_8 = INPUT_OUT ? binary_to_bcd_converter_2_p1 : 8'bz;  // Controlled_Buffer controlled_buffer_1
  STEP_COUNTER step_counter_1 (
    .RESET(or_1_out), .CLOCK(not_1_out), .STEP_COUNTER_OUT({step_counter_1_step_counter_out[3], STEP_COUNT}));
  REGISTER_A register_a_1 (
    .DATA_IN(alu_1_out_8), .ENB_REG_A_IN(REG_A_IN), .ENB_REG_A_OUT(REG_A_OUT), .CLOCK(clk_1_clk_out),
    .RESET(RESET), .REG_A_OUT(ALU_A));  // open: ALWAYS_OUT
  REGISTER_B register_b_1 (
    .DATA_IN(alu_1_out_8), .ENB_REG_A_IN(REG_B_IN), .ENB_REG_A_OUT(REG_B_OUT), .CLOCK(clk_1_clk_out),
    .RESET(RESET), .REG_A_OUT(ALU_B));  // open: ALWAYS_OUT
  REGISTER_OUTPUT register_output_1 (
    .DATA_IN(alu_1_out_8), .ENB_REG_IN(OUT_REG_IN), .ENB_REG_OUT(OUT_REG_OUT), .CLOCK(clk_1_clk_out),
    .RESET(RESET), .ALWAYS_OUT(register_output_1_always_out), .REG_OUT(alu_1_out_8));
  REGISTER_INSTRUCTION register_instruction_1 (
    .DATA_IN(alu_1_out_8), .CLOCK(clk_1_clk_out), .RESET(RESET), .REG_OUT(INST_LOAD));  // open: ENB_REG_IN, ENB_REG_OUT, ALWAYS_OUT
  or or_1 (or_1_out, RESET, decoder_1_out5);
  not not_1 (not_1_out, clk_1_clk_out);
  _7_Segment_Display u_7_segment_display_1 ();  // open: g, f, a, b, e, d, c, dp
  // BCD_to_7_Segment_decoder bcd_to_7_segment_decoder_1: pin names not known
  _7_Segment_Display u_7_segment_display_2 ();  // open: g, f, a, b, e, d, c, dp
  _7_Segment_Display u_7_segment_display_3 ();  // open: g, f, a, b, e, d, c, dp
  // BCD_to_7_Segment_decoder bcd_to_7_segment_decoder_2: pin names not known
  // BCD_to_7_Segment_decoder bcd_to_7_segment_decoder_3: pin names not known
  // Binary_to_BCD_converter #(.binvalue(8)) binary_to_bcd_converter_1: pin names not known; wires that end beside it: register_output_1_always_out
  _7_Segment_Display u_7_segment_display_4 ();  // open: g, f, a, b, e, d, c, dp
  // BCD_to_7_Segment_decoder bcd_to_7_segment_decoder_4: pin names not known
  // Binary_to_BCD_converter #(.binvalue(8)) binary_to_bcd_converter_2: pin names not known; wires that end beside it: binary_to_bcd_converter_2_p1
  _7_Segment_Display u_7_segment_display_5 ();  // open: g, f, a, b, e, d, c, dp
  // BCD_to_7_Segment_decoder bcd_to_7_segment_decoder_5: pin names not known
  _7_Segment_Display u_7_segment_display_6 ();  // open: g, f, a, b, e, d, c, dp
  // BCD_to_7_Segment_decoder bcd_to_7_segment_decoder_6: pin names not known
endmodule

module CLK (
  input  CLK_IN,
  input  CLK_ENB,
  input  MANUAL,
  input  STOP,
  output CLK_OUT
);

  wire and_1_out, and_2_out, not_1_out, not_2_out, or_1_out;

  not not_1 (not_1_out, CLK_ENB);
  and and_1 (and_1_out, CLK_IN, CLK_ENB);
  and and_2 (and_2_out, not_1_out, MANUAL);
  not not_2 (not_2_out, STOP);
  or or_1 (or_1_out, and_1_out, and_2_out);
  and and_3 (CLK_OUT, or_1_out, not_2_out);
endmodule

module PC (
  input  RESET,
  input  JUMP,
  input  COUNTER_ENB,
  input  CLK,
  input  [15:0] ADD_IN,
  input  OUT_ENB,
  output [15:0] ALWAYS_OUT,
  output [15:0] PC_OUT
);

  Counter #(.max('hffff), .width(16)) counter_1 (
    .clr(RESET), .load(JUMP), .up(COUNTER_ENB), .count(COUNTER_ENB), .clk(CLK), .D(ADD_IN), .Q(ALWAYS_OUT));  // open: carry
  assign PC_OUT = OUT_ENB ? ALWAYS_OUT : 16'bz;  // Controlled_Buffer controlled_buffer_1
endmodule

module REGISTER_A (
  input  [7:0] DATA_IN,
  input  ENB_REG_A_IN,
  input  ENB_REG_A_OUT,
  input  CLOCK,
  input  RESET,
  output [7:0] ALWAYS_OUT,
  output [7:0] REG_A_OUT
);

  Register register_1 (.D(DATA_IN), .en(ENB_REG_A_IN), .clk(CLOCK), .Q(ALWAYS_OUT), .clr(RESET));
  assign REG_A_OUT = ENB_REG_A_OUT ? ALWAYS_OUT : 8'bz;  // Controlled_Buffer controlled_buffer_1
endmodule

module REGISTER_B (
  input  [7:0] DATA_IN,
  input  ENB_REG_A_IN,
  input  ENB_REG_A_OUT,
  input  CLOCK,
  input  RESET,
  output [7:0] ALWAYS_OUT,
  output [7:0] REG_A_OUT
);

  Register register_1 (.D(DATA_IN), .en(ENB_REG_A_IN), .clk(CLOCK), .Q(ALWAYS_OUT), .clr(RESET));
  assign REG_A_OUT = ENB_REG_A_OUT ? ALWAYS_OUT : 8'bz;  // Controlled_Buffer controlled_buffer_1
endmodule

module REGISTER_OUTPUT (
  input  [7:0] DATA_IN,
  input  ENB_REG_IN,
  input  ENB_REG_OUT,
  input  CLOCK,
  input  RESET,
  output [7:0] ALWAYS_OUT,
  output [7:0] REG_OUT
);

  Register register_1 (.D(DATA_IN), .en(ENB_REG_IN), .clk(CLOCK), .Q(ALWAYS_OUT), .clr(RESET));
  assign REG_OUT = ENB_REG_OUT ? ALWAYS_OUT : 8'bz;  // Controlled_Buffer controlled_buffer_1
endmodule

module REGISTER_INSTRUCTION (
  input  [7:0] DATA_IN,
  input  ENB_REG_IN,
  input  ENB_REG_OUT,
  input  CLOCK,
  input  RESET,
  output [7:0] ALWAYS_OUT,
  output [7:0] REG_OUT
);

  Register register_1 (.D(DATA_IN), .en(ENB_REG_IN), .clk(CLOCK), .Q(ALWAYS_OUT), .clr(RESET));
  assign REG_OUT = ENB_REG_OUT ? ALWAYS_OUT : 8'bz;  // Controlled_Buffer controlled_buffer_1
endmodule

module ALU (
  input  C_IN,
  input  [2:0] OPERATION,
  input  [7:0] A_IN,
  input  [7:0] B_IN,
  input  ENB_OUT,
  output Z_OUT,
  output [7:0] out_7,
  output [7:0] out_8,
  output C_OUT,
  output SG_OUT,
  output OV_OUT
);

  wire adder_1_cout, adder_2_cout, and_1_out, and_2_out, not_1_out, subtractor_1_bout, xor_1_out, xor_2_out;
  wire [7:0] adder_1_out, adder_2_out, divider_1_out, multiplier_1_out, subtractor_1_out, subtractor_2_out;

  xor xor_1 (xor_1_out, B_IN[7], A_IN[7]);
  not not_1 (not_1_out, xor_1_out);
  and and_1 (and_1_out, not_1_out, xor_2_out);
  xor xor_2 (xor_2_out, A_IN[7], out_7[7]);
  and and_2 (and_2_out, xor_2_out, xor_1_out);
  Adder adder_1 (.a(A_IN), .b(B_IN), .out(adder_1_out), .cin(C_IN), .cout(adder_1_cout));
  Subtractor subtractor_1 (.a(A_IN), .b(B_IN), .out(subtractor_1_out), .bout(subtractor_1_bout));  // open: bin
  Multiplier multiplier_1 (.a(A_IN), .b(B_IN), .out(multiplier_1_out));  // open: cin, cout
  Divider divider_1 (.a(A_IN), .b(B_IN), .out(divider_1_out));  // open: upper, rem
  Adder adder_2 (.a(A_IN), .b(8'h1), .out(adder_2_out), .cout(adder_2_cout));  // open: cin
  Subtractor subtractor_2 (.a(A_IN), .b(8'h1), .out(subtractor_2_out));  // open: bin, bout
  Multiplexer #(.select(3), .width(8)) multiplexer_1 (
    .in0({8{1'b0}}), .in1(adder_1_out), .in2(subtractor_1_out), .in3(multiplier_1_out), .in4(divider_1_out),
    .in5(adder_2_out), .in6(subtractor_2_out), .out(out_7), .sel(OPERATION));  // open: in7
  Multiplexer #(.select(3)) multiplexer_2 (
    .in0(1'b0), .in1(adder_1_cout), .in2(subtractor_1_bout), .in5(adder_2_cout), .out(C_OUT), .sel(OPERATION));  // open: in3, in4, in6, in7
  Multiplexer #(.select(3)) multiplexer_3 (
    .in0(1'b0), .in1(and_1_out), .in2(and_2_out), .out(OV_OUT), .sel(OPERATION));  // open: in3, in4, in5, in6, in7
  nor nor_1 (Z_OUT, out_7[0], out_7[1], out_7[2], out_7[3], out_7[4], out_7[5], out_7[6], out_7[7]);
  assign out_8 = ENB_OUT ? out_7 : 8'bz;  // Controlled_Buffer controlled_buffer_1

  assign SG_OUT = out_7[7];
endmodule

module FLAGS_REGISTER (
  input  Z_ALU,
  input  SG_ALU,
  input  FLAG_EN,
  input  CLK,
  input  OV_ALU,
  input  C_ALU,
  output Z_OUT,
  output SG_OUT,
  output OV_OUT,
  output C_OUT
);

  wire multiplexer_1_out, multiplexer_2_out, multiplexer_3_out, multiplexer_4_out;

  Multiplexer multiplexer_1 (.in0(Z_OUT), .out(multiplexer_1_out), .sel(FLAG_EN));  // open: in1
  D_Flip_Flop ZERO_FLAG (.D(multiplexer_1_out), .clk(CLK), .Q(Z_OUT));  // open: Qn, preset, reset
  Multiplexer multiplexer_2 (.in0(C_OUT), .in1(C_ALU), .out(multiplexer_2_out), .sel(FLAG_EN));
  D_Flip_Flop CARRY_OUT (.D(multiplexer_2_out), .clk(CLK), .Q(C_OUT));  // open: Qn, preset, reset
  Multiplexer multiplexer_3 (.in0(SG_OUT), .in1(SG_ALU), .out(multiplexer_3_out), .sel(FLAG_EN));
  D_Flip_Flop SIGN_FLAG (.D(multiplexer_3_out), .clk(CLK), .Q(SG_OUT));  // open: Qn, preset, reset
  Multiplexer multiplexer_4 (.in0(OV_OUT), .in1(OV_ALU), .out(multiplexer_4_out), .sel(FLAG_EN));
  D_Flip_Flop OVERFLOW_FLAG (.D(multiplexer_4_out), .clk(CLK), .Q(OV_OUT));  // open: Qn, preset, reset
endmodule

module MAR (
  input  [15:0] DATA_IN,
  input  ENB_IN,
  input  CLK,
  input  RESET,
  input  ENB_OUT,
  output [15:0] ALWAYS_OUT,
  output [15:0] MAR_OUT
);

  Register #(.width(16)) register_1 (.D(DATA_IN), .en(ENB_IN), .clk(CLK), .Q(ALWAYS_OUT), .clr(RESET));
  assign MAR_OUT = ENB_OUT ? ALWAYS_OUT : 16'bz;  // Controlled_Buffer controlled_buffer_1
endmodule

module RAM_MEMORY (
  input  [15:0] ADD_IN,
  input  WRITE_ENB,
  input  CLK,
  input  [7:0] DATA_IN,
  output [7:0] out_5
);

  RAM #(.addrWidth(16), .enables("line")) ram_1 (.addr(ADD_IN), .we(WRITE_ENB), .clk(CLK), .din(DATA_IN), .dout(out_5));
endmodule

module CONTROL_UNIT (
  input  [7:0] in_1,
  input  [2:0] STEP_COUNT,
  output [2:0] ALU_OP,
  output JUMP,
  output ALU_ON,
  output PC_ON,
  output REG_A_IN,
  output REG_B_IN,
  output MAR_IN,
  output INS_REG_IN,
  output OUT_REG_IN,
  output REG_A_OUT,
  output REG_B_OUT,
  output MAR_OUT,
  output INS_REG_OUT,
  output OUT_REG_OUT,
  output INPUT_OUT,
  output PC_OUT,
  output RAM_READ_ENB
);

  wire ALU, demultiplexer_5_out0, demultiplexer_6_out0, JUMP_t, LOAD, MAR_IN_t, or_5_out, or_6_out,
       OUT_REG_IN_t, PC_ON_ALU, PC_ON_LOAD_REG, PC_ON_MAR_IN, PC_ON_RAM_IN, PC_ON_WRITE_REG, RAM,
       REG_A_OUT_t, REG_B_OUT_t, REG_IN, REG_OU;

  Decoder #(.enable("false"), .select(4)) decoder_1 (
    .out1(REG_IN), .out2(ALU), .out3(REG_OU), .out4(LOAD), .out5(MAR_IN_t), .out6(JUMP_t), .out7(RAM),
    .sel(in_1[7:4]));  // open: out0, out8, out9, out10, out11, out12, out13, out14, out15
  Demultiplexer #(.select(3)) demultiplexer_1 (
    .out0(ALU_ON), .out4(PC_ON_ALU), .in(ALU), .sel(STEP_COUNT));  // open: out1, out2, out3, out5, out6, out7
  or or_1 (OUT_REG_IN, OUT_REG_IN_t, ALU_ON);
  or or_2 (REG_A_OUT, REG_A_OUT_t, ALU_ON);
  or or_3 (REG_B_OUT, REG_B_OUT_t, ALU_ON);
  Demultiplexer #(.select(3)) demultiplexer_2 (
    .out0(JUMP), .in(JUMP_t), .sel(STEP_COUNT));  // open: out1, out2, out3, out4, out5, out6, out7
  or or_4 (PC_ON, PC_ON_ALU, PC_ON_MAR_IN, PC_ON_RAM_IN, PC_ON_WRITE_REG, PC_ON_LOAD_REG);
  Demultiplexer #(.select(3)) demultiplexer_3 (
    .out0(RAM_READ_ENB), .out4(PC_ON_RAM_IN), .in(RAM), .sel(STEP_COUNT));  // open: out1, out2, out3, out5, out6, out7
  Demultiplexer #(.select(3)) demultiplexer_4 (
    .out0(MAR_IN), .out4(PC_ON_MAR_IN), .in(MAR_IN_t), .sel(STEP_COUNT));  // open: out1, out2, out3, out5, out6, out7
  or or_5 (or_5_out, LOAD, REG_IN);
  Demultiplexer #(.select(3)) demultiplexer_5 (
    .out0(demultiplexer_5_out0), .out4(PC_ON_WRITE_REG), .in(or_5_out), .sel(STEP_COUNT));  // open: out1, out2, out3, out5, out6, out7
  or or_6 (or_6_out, LOAD, REG_OU);
  Demultiplexer #(.select(3)) demultiplexer_6 (
    .out0(demultiplexer_6_out0), .out4(PC_ON_LOAD_REG), .in(or_6_out), .sel(STEP_COUNT));  // open: out1, out2, out3, out5, out6, out7
  Decoder #(.select(2)) decoder_2 (
    .out0(REG_A_IN), .out1(REG_B_IN), .out2(OUT_REG_IN_t), .out3(INS_REG_IN), .sel(in_1[1:0]),
    .en(demultiplexer_5_out0));
  Decoder #(.select(2)) decoder_3 (
    .out0(REG_A_OUT_t), .out1(REG_B_OUT_t), .out2(OUT_REG_OUT), .out3(INS_REG_OUT), .sel(in_1[3:2]),
    .en(demultiplexer_6_out0));
  assign INPUT_OUT = REG_IN ? demultiplexer_5_out0 : 1'bz;  // Controlled_Buffer controlled_buffer_1

  assign ALU_OP = in_1[2:0];
  assign MAR_OUT = JUMP;
  assign PC_OUT = PC_ON;

  // Other names for the same wires on the sheet: ALU_A_OUT = ALU_ON; ALU_B_OUT = ALU_ON; ALU_OUT_IN = ALU_ON;
  //   SELECTOR[3:0] = in_1[3:0]; JUMP_ENB = JUMP; MAR_IN_ENB = MAR_IN; PC_OUT_ENB = PC_ON;
  //   STEP_CPOUNTER_IN[2:0] = STEP_COUNT
endmodule

module STEP_COUNTER (
  input  RESET,
  input  CLOCK,
  output [3:0] STEP_COUNTER_OUT
);

  Counter #(.max('hf), .width(4)) counter_1 (
    .clr(RESET), .up(1'b1), .count(1'b1), .clk(CLOCK), .Q(STEP_COUNTER_OUT));  // open: load, D, carry
endmodule
